// Logisim project alu.circ as structural Verilog: 7 circuits, main circuit halfAdder
module halfAdder (
  input  A,
  input  B,
  output C,
  output S
);

  and and_1 (C, B, A);
  xor xor_1 (S, B, A);
endmodule

module fullAdder (
  input  A,
  input  B,
  input  Ci,
  output Co,
  output S
);

  wire halfadder_1_c, halfadder_1_s, halfadder_2_c;

  halfAdder halfadder_1 (.A(A), .B(B), .C(halfadder_1_c), .S(halfadder_1_s));
  halfAdder halfadder_2 (.A(halfadder_1_s), .B(Ci), .C(halfadder_2_c), .S(S));
  or or_1 (Co, halfadder_1_c, halfadder_2_c);
endmodule

module fullAdder32 (
  input  [31:0] A32,
  input  [31:0] B32,
  input  Ci,
  output [31:0] S32,
  output Co
);

  wire fulladder16_1_co;

  fullAdder16 fulladder16_1 (.A16(A32[15:0]), .B16(B32[15:0]), .Ci(Ci), .Co(fulladder16_1_co), .S16(S32[15:0]));
  fullAdder16 fulladder16_2 (.A16(A32[31:16]), .B16(B32[31:16]), .Ci(fulladder16_1_co), .Co(Co), .S16(S32[31:16]));
endmodule

module fullAdder4 (
  input  [3:0] A,
  input  [3:0] B,
  input  Ci,
  output Co,
  output [3:0] S
);

  wire fulladder_1_co, fulladder_2_co, fulladder_3_co;

  fullAdder fulladder_1 (.A(A[0]), .B(B[0]), .Ci(Ci), .Co(fulladder_1_co), .S(S[0]));
  fullAdder fulladder_2 (.A(A[2]), .B(B[2]), .Ci(fulladder_3_co), .Co(fulladder_2_co), .S(S[2]));
  fullAdder fulladder_3 (.A(A[1]), .B(B[1]), .Ci(fulladder_1_co), .Co(fulladder_3_co), .S(S[1]));
  fullAdder fulladder_4 (.A(A[3]), .B(B[3]), .Ci(fulladder_2_co), .Co(Co), .S(S[3]));
endmodule

module fullAdder16 (
  input  [15:0] A16,
  input  [15:0] B16,
  input  Ci,
  output Co,
  output [15:0] S16
);

  wire fulladder4_1_co, fulladder4_2_co, fulladder4_3_co;

  fullAdder4 fulladder4_1 (.A(A16[3:0]), .B(B16[3:0]), .Ci(Ci), .Co(fulladder4_1_co), .S(S16[3:0]));
  fullAdder4 fulladder4_2 (.A(A16[11:8]), .B(B16[11:8]), .Ci(fulladder4_3_co), .Co(fulladder4_2_co), .S(S16[11:8]));
  fullAdder4 fulladder4_3 (.A(A16[7:4]), .B(B16[7:4]), .Ci(fulladder4_1_co), .Co(fulladder4_3_co), .S(S16[7:4]));
  fullAdder4 fulladder4_4 (.A(A16[15:12]), .B(B16[15:12]), .Ci(fulladder4_2_co), .Co(Co), .S(S16[15:12]));
endmodule

module alu (
  input  [31:0] A32,
  input  [31:0] B32,
  input  [3:0] OP4,
  output CF,
  output [31:0] F32,
  output SF,
  output ZF
);

  wire comparator_1_lt, comparator_2_lt, fulladder32_1_co, subtractor_1_bout;
  wire [4:0] bit_extender_1_out;
  wire [31:0] and_1_out, bit_extender_2_out, divider_1_out, fulladder32_1_s32, multiplier_1_cout,
       multiplier_1_out, not_1_out, or_1_out, shifter_1_out, subtractor_1_out, xor_1_out;

  assign and_1_out = A32 & B32;  // AND_Gate and_1, 32 bits wide
  assign or_1_out = A32 | B32;  // OR_Gate or_1, 32 bits wide
  assign not_1_out = ~or_1_out;  // NOT_Gate not_1, 32 bits wide
  assign xor_1_out = A32 ^ B32;  // XOR_Gate xor_1, 32 bits wide
  Subtractor #(.width(32)) subtractor_1 (
    .a(A32), .b(B32), .out(subtractor_1_out), .bin(1'b0), .bout(subtractor_1_bout));
  Comparator #(.width(32)) comparator_1 (.a(A32), .b(B32), .lt(comparator_1_lt));  // open: gt, eq
  Bit_Extender #(.in_width(32), .out_width(5), .\type ("zero")) bit_extender_1 (.in(A32), .out(bit_extender_1_out));
  Multiplier #(.width(32)) multiplier_1 (
    .a(A32), .b(B32), .out(multiplier_1_out), .cout(multiplier_1_cout));  // open: cin
  Divider #(.width(32)) divider_1 (.a(A32), .b(B32), .out(divider_1_out));  // open: upper, rem
  assign bit_extender_2_out = {{31{1'b0}}, comparator_1_lt};  // Bit_Extender bit_extender_2
  Shifter #(.width(32)) shifter_1 (.in(B32), .\dist (bit_extender_1_out), .out(shifter_1_out));
  Comparator #(.width(32)) comparator_2 (.a({32{1'b0}}), .b(multiplier_1_cout), .lt(comparator_2_lt));  // open: gt, eq
  fullAdder32 fulladder32_1 (.A32(A32), .B32(B32), .Ci(1'b0), .S32(fulladder32_1_s32), .Co(fulladder32_1_co));
  Multiplexer #(.select(4), .width(32)) multiplexer_1 (
    .in0(and_1_out), .in1(or_1_out), .in2(xor_1_out), .in3(not_1_out), .in4(fulladder32_1_s32),
    .in5(subtractor_1_out), .in6(bit_extender_2_out), .in7(shifter_1_out), .in8(multiplier_1_out),
    .in9(divider_1_out), .out(F32), .sel(OP4));  // open: in10, in11, in12, in13, in14, in15
  Multiplexer #(.select(4)) multiplexer_2 (
    .in3(fulladder32_1_co), .in4(subtractor_1_bout), .in8(comparator_2_lt), .out(CF), .sel(OP4));  // open: in0, in1, in2, in5, in6, in7, in9, in10, in11, in12, in13, in14, in15
  BitSelector #(.width(32)) bitselector_1 (.in(F32), .out(SF), .sel({5{1'b1}}));
  Comparator #(.width(32)) comparator_3 (.a({32{1'b0}}), .b(F32), .eq(ZF));  // open: gt, lt
endmodule

module alu_extend (
  input  [31:0] A32,
  input  [31:0] B32,
  input  [3:0] OP4,
  output [31:0] Result1,
  output [31:0] Result2
);

  wire comparator_1_lt, comparator_2_lt, fulladder32_1_p4;
  wire [4:0] bitselector_1_out, bitselector_2_out, bitselector_3_out;
  wire [31:0] and_1_out, bit_extender_1_out, bit_extender_2_out, divider_1_out, divider_1_rem,
       fulladder32_1_p6, multiplier_1_cout, multiplier_1_out, nor_1_out, or_1_out, shifter_1_out,
       shifter_2_out, shifter_3_out, subtractor_1_out, xor_1_out;

  BitSelector #(.group(5), .width(32)) bitselector_1 (.in(A32), .out(bitselector_1_out), .sel(3'b000));
  BitSelector #(.group(5), .width(32)) bitselector_2 (.in(A32), .out(bitselector_2_out), .sel(3'b000));
  BitSelector #(.group(5), .width(32)) bitselector_3 (.in(A32), .out(bitselector_3_out), .sel(3'b000));
  Subtractor #(.width(32)) subtractor_1 (.a(A32), .b(B32), .out(subtractor_1_out), .bin(1'b0));  // open: bout
  assign and_1_out = A32 & B32;  // AND_Gate and_1, 32 bits wide
  assign or_1_out = A32 | B32;  // OR_Gate or_1, 32 bits wide
  assign xor_1_out = A32 ^ B32;  // XOR_Gate xor_1, 32 bits wide
  assign nor_1_out = ~(A32 | B32);  // NOR_Gate nor_1, 32 bits wide
  Comparator #(.width(32)) comparator_1 (.a(A32), .b(B32), .lt(comparator_1_lt));  // open: gt, eq
  Comparator #(.mode("unsigned"), .width(32)) comparator_2 (.a(A32), .b(B32), .lt(comparator_2_lt));  // open: gt, eq
  Shifter #(.width(32)) shifter_1 (.in(B32), .\dist (bitselector_1_out), .out(shifter_1_out));
  Shifter #(.shift("ar"), .width(32)) shifter_2 (.in(B32), .\dist (bitselector_2_out), .out(shifter_2_out));
  Shifter #(.shift("lr"), .width(32)) shifter_3 (.in(B32), .\dist (bitselector_3_out), .out(shifter_3_out));
  Multiplier #(.width(32)) multiplier_1 (
    .a(A32), .b(B32), .out(multiplier_1_out), .cout(multiplier_1_cout));  // open: cin
  Divider #(.width(32)) divider_1 (.a(A32), .b(B32), .out(divider_1_out), .upper({32{1'b0}}), .rem(divider_1_rem));
  assign bit_extender_1_out = {{31{1'b0}}, comparator_1_lt};  // Bit_Extender bit_extender_1
  assign bit_extender_2_out = {{31{1'b0}}, comparator_2_lt};  // Bit_Extender bit_extender_2
  // fullAdder32 fulladder32_1: pin names not known; wires that end beside it: A32, B32, 1'b0, fulladder32_1_p4, fulladder32_1_p4, fulladder32_1_p6
  Multiplexer #(.select(4), .width(32)) multiplexer_1 (
    .in0(shifter_1_out), .in1(shifter_2_out), .in2(shifter_3_out), .in3(multiplier_1_out),
    .in4(divider_1_out), .in5(fulladder32_1_p6), .in6(subtractor_1_out), .in7(and_1_out), .in8(or_1_out),
    .in9(xor_1_out), .in10(nor_1_out), .in11(bit_extender_1_out), .in12(bit_extender_2_out), .out(Result1),
    .sel(OP4));  // open: in13, in14, in15
  Multiplexer #(.select(4), .width(32)) multiplexer_2 (
    .in3(multiplier_1_cout), .in4(divider_1_rem), .out(Result2), .sel(OP4));  // open: in0, in1, in2, in5, in6, in7, in8, in9, in10, in11, in12, in13, in14, in15
endmodule
