// Logisim project cpu.circ as structural Verilog: 25 circuits, main circuit cpu
module cpu (
  input  in_1,
  input  in_2,
  input  in_3,
  input  in_4
);

  wire ID_clk, isUnsigned, MEM_clk, memorycontrolunit_1_be0, memorycontrolunit_1_be1,
       memorycontrolunit_1_be2, memorycontrolunit_1_be3, memorycontrolunit_1_mem_clk,
       memorycontrolunit_1_memrden, memorycontrolunit_1_memwren, MemRd, MemWr, PC_Branch, PCWr, W_En;
  wire [1:0] BranchMode, BranchtoPC, JumpMode, MemSMode, PC_Src, RegInstType, WBSel;
  wire [2:0] MemLMode;
  wire [3:0] ALUOp, ALUSel;
  wire [4:0] instdecoder_1_rd, instdecoder_1_rs, instdecoder_1_rt, instdecoder_1_shamt, regselunit_1_r_reg1,
       regselunit_1_r_reg2, regselunit_1_w_reg;
  wire [5:0] instdecoder_1_func, instdecoder_1_op;
  wire [15:0] adder_1_out, ImmtoPC, memorycontrolunit_1_mem_addr, programcounter_1_pc_out, shifter_1_out;
  wire [25:0] JInsttoPC;
  wire [31:0] alu_extend_1_result1, alu_extend_1_result2, aluselunit_1_opnuma, aluselunit_1_opnumb,
       memorycontrolunit_1_memr_data, memorycontrolunit_1_memw_data, ram_1_dout, register_group32_1_r_data2,
       RegtoPC, rom_1_data, writebackunit_1_toreg;

  ProgramCounter programcounter_1 (
    .clk(ID_clk), .PCWr(PCWr), .PC_Branch(PC_Branch), .PC_JumpMode(JumpMode), .PC_Src(PC_Src),
    .BranchtoPC(BranchtoPC), .ImmtoPC(ImmtoPC), .JInsttoPC(JInsttoPC), .RegtoPC(RegtoPC),
    .PC_Out(programcounter_1_pc_out));
  // Probe on programcounter_1_pc_out
  Shifter #(.shift("lr"), .width(16)) shifter_1 (.in(programcounter_1_pc_out), .\dist (4'b0010), .out(shifter_1_out));
  ROM #(.addrWidth(16), .dataWidth(32)) rom_1 (.addr(shifter_1_out), .data(rom_1_data));
  ClkUnit clkunit_1 (
    .Reset(in_1), .EnClk(in_2), .AM_Switch(in_3), .Manual_Step(in_4), .clk1(ID_clk), .clk3(MEM_clk));  // open: clk2, clk4, clk5
  InstDecoder instdecoder_1 (
    .Inst(rom_1_data), .J_Addr(JInsttoPC), .I_Imm(ImmtoPC), .Func(instdecoder_1_func),
    .Shamt(instdecoder_1_shamt), .Rd(instdecoder_1_rd), .Rt(instdecoder_1_rt), .Rs(instdecoder_1_rs),
    .Op(instdecoder_1_op));
  CtrlUnit ctrlunit_1 (
    .OpCode(instdecoder_1_op), .Funct(instdecoder_1_func), .PCWr(PCWr), .PC_Branch(PC_Branch),
    .PC_Src(PC_Src), .W_En(W_En), .RegInstType(RegInstType), .JumpMode(JumpMode), .isUnsigned(isUnsigned),
    .ALUOp(ALUOp), .ALUSel(ALUSel), .BranchMode(BranchMode), .MemRd(MemRd), .MemWr(MemWr),
    .MemSMode(MemSMode), .MemLMode(MemLMode), .WBSel(WBSel));  // open: MF_SpReg, MF_Mode
  regSelUnit regselunit_1 (
    .RegInstType(RegInstType), .RegJumpMode(JumpMode), .Rd(instdecoder_1_rd), .Rt(instdecoder_1_rt),
    .Rs(instdecoder_1_rs), .W_Reg(regselunit_1_w_reg), .R_Reg1(regselunit_1_r_reg1),
    .R_Reg2(regselunit_1_r_reg2));
  // Probe on PC_Src
  // Probe on ALUOp
  Adder #(.width(16)) adder_1 (.a(programcounter_1_pc_out), .b(16'h3004), .out(adder_1_out));  // open: cin, cout
  register_group32 register_group32_1 (
    .clk(ID_clk), .W_En(W_En), .W_data(writebackunit_1_toreg), .W_Reg(regselunit_1_w_reg),
    .R_Reg1(regselunit_1_r_reg1), .R_Reg2(regselunit_1_r_reg2), .R_data1(RegtoPC),
    .R_data2(register_group32_1_r_data2));
  // Probe on aluselunit_1_opnuma
  ALUSelUnit aluselunit_1 (
    .ALUSel(ALUSel), .PC(adder_1_out), .RegR1(RegtoPC), .RegR2(register_group32_1_r_data2),
    .InstImm(ImmtoPC), .Shamt(instdecoder_1_shamt), .OpNumA(aluselunit_1_opnuma), .OpNumB(aluselunit_1_opnumb));
  // Probe on alu_extend_1_result1
  alu_extend alu_extend_1 (
    .A32(aluselunit_1_opnuma), .B32(aluselunit_1_opnumb), .OP4(ALUOp), .Result1(alu_extend_1_result1),
    .Result2(alu_extend_1_result2));
  // Probe on BranchMode
  MemoryControlUnit memorycontrolunit_1 (
    .clk(MEM_clk), .MemRd(MemRd), .MemWr(MemWr), .MemSMode(MemSMode), .MemLMode(MemLMode),
    .ALU_Res1(alu_extend_1_result1), .ALU_Res2(alu_extend_1_result2), .RegtoMem(register_group32_1_r_data2),
    .MemOut(ram_1_dout), .Mem_Clk(memorycontrolunit_1_mem_clk), .MemRdEn(memorycontrolunit_1_memrden),
    .MemWrEn(memorycontrolunit_1_memwren), .Mem_Addr(memorycontrolunit_1_mem_addr),
    .MemW_data(memorycontrolunit_1_memw_data), .BE3(memorycontrolunit_1_be3), .BE2(memorycontrolunit_1_be2),
    .BE1(memorycontrolunit_1_be1), .BE0(memorycontrolunit_1_be0), .MemR_data(memorycontrolunit_1_memr_data));
  RAM #(.addrWidth(16), .byteenables("byteEnables"), .dataWidth(32)) ram_1 (
    .addr(memorycontrolunit_1_mem_addr), .we(memorycontrolunit_1_memwren), .oe(memorycontrolunit_1_memrden),
    .clk(memorycontrolunit_1_mem_clk), .din(memorycontrolunit_1_memw_data), .dout(ram_1_dout),
    .be3(memorycontrolunit_1_be3), .be2(memorycontrolunit_1_be2), .be1(memorycontrolunit_1_be1),
    .be0(memorycontrolunit_1_be0));
  // Probe on BranchtoPC
  BranchControlUnit branchcontrolunit_1 (
    .BranchMode(BranchMode), .ALU_Res1(alu_extend_1_result1), .BranchtoPC(BranchtoPC));
  // Probe on memorycontrolunit_1_mem_addr
  // Probe on memorycontrolunit_1_memr_data
  WriteBackUnit writebackunit_1 (
    .WBSel(WBSel), .ALU_Res1(alu_extend_1_result1), .ALU_Res2(alu_extend_1_result2),
    .Mem_data(memorycontrolunit_1_memr_data), .ToReg(writebackunit_1_toreg));

  // Other names for the same wires on the sheet: IF_clk = ID_clk

  // Notes on the sheet:
  //   contents of rom_1 (hex, n*v repeats v):
  //   200501ff ac050000 a4050006 a005000b 24050002 ac05000c a52820 ac050010 a52821 ac050014 a52822
  //   ac050018 20050040 20060020 a62823 ac05001c 20050003 52880 ac050020 52882 ac050024 20050005 20060002
  //   c52804 ac050028 c52806 ac05002c 20050007 52843 ac050030 20060001 c52807 ac050034 200501ff ac050038
  //   ac05003c 20050005 a52824 ac050040 30a50000 ac050044 20050005 20060002 a63825 ac070048 a63827
  //   ac07004c 34a70002 ac070050 a63826 ac070054 38a70002 ac070058 200501ff a405005e 8c05005c ac050060
  //   8405005e ac050064 8000c00
endmodule

module cpu_Pipeline (
  input  in_1,
  input  in_2,
  input  in_3,
  input  in_4
);

  wire clk1, clk2, clk3, clk4, clk5, EX_clk, ex_reg_1_weno, ID_clk1, ID_clk2, id_reg_1_mro, id_reg_1_mwo,
       id_reg_1_weno, IF_clk, isUnsigned, IUO, MEM_clk, memorycontrolunit_1_be0, memorycontrolunit_1_be1,
       memorycontrolunit_1_be2, memorycontrolunit_1_be3, memorycontrolunit_1_mem_clk,
       memorycontrolunit_1_memrden, memorycontrolunit_1_memwren, MemRd, MemWr, MRO, MWO, or_1_out, PauseEx,
       PauseID, PauseIF, PauseWB, PC_Branch, PCBO, PCWO, PCWr, W_En, WENO;
  wire [1:0] BMO, BranchMode, BranchtoPC, BTPO, EX_InstType, ex_reg_1_jmo, ex_reg_1_wbso, ID_InstType,
       id_reg_1_msmo, id_reg_1_wbso, JMO, JumpMode, MemSMode, MSMO, PC_Src, PCSO, RegInstType, WBSel, WBSO;
  wire [2:0] id_reg_1_mlmo, MemLMode, MLMO;
  wire [3:0] ALUOp, ALUOPO, ALUSel, ALUSELO;
  wire [4:0] EX_WReg, id_reg_1_wro, ID_RReg1, ID_RReg2, instdecoder_1_rd, instdecoder_1_rs, instdecoder_1_rt,
       regselunit_1_r_reg1, regselunit_1_r_reg2, Shamt, SHAMTO, W_Reg, WRO;
  wire [5:0] instdecoder_1_func, instdecoder_1_op;
  wire [15:0] adder_1_out, IIMO, IMTPO, InstImm, memorycontrolunit_1_mem_addr, PC, PCO,
       programcounter_1_pc_out, shifter_1_out;
  wire [25:0] JInsttoPC, JITPO;
  wire [31:0] ALUResult1, ALUResult2, aluselunit_1_opnuma, aluselunit_1_opnumb, Ex_ALUR1O, Ex_ALUR2O,
       id_reg_1_rtmo, if_reg_1_inst_out, memorycontrolunit_1_memw_data, MemtoWB, MTWBO, R_data1, R_data2,
       ram_1_dout, RDT1O, RDT2O, rom_1_data, RTMO, RTPO, WB_ALUR1O, WB_ALUR2O, writebackunit_1_toreg;

  // Probe on programcounter_1_pc_out
  ProgramCounter programcounter_1 (
    .clk(IF_clk), .PCWr(PCWO), .PC_Branch(PCBO), .PC_JumpMode(JMO), .PC_Src(PCSO), .BranchtoPC(BTPO),
    .ImmtoPC(IMTPO), .JInsttoPC(JITPO), .RegtoPC(RTPO), .PC_Out(programcounter_1_pc_out));
  Shifter #(.shift("lr"), .width(16)) shifter_1 (.in(programcounter_1_pc_out), .\dist (4'b0010), .out(shifter_1_out));
  ROM #(.addrWidth(16), .dataWidth(32)) rom_1 (.addr(shifter_1_out), .data(rom_1_data));
  ClkUnit clkunit_1 (
    .Reset(in_1), .EnClk(in_2), .AM_Switch(in_3), .Manual_Step(in_4), .clk1(clk1), .clk2(clk2), .clk3(clk3),
    .clk4(clk4), .clk5(clk5));
  ConflictHandler conflicthandler_1 (
    .clk(clk1), .EX_WReg(EX_WReg), .ID_RReg1(ID_RReg1), .ID_RReg2(ID_RReg2), .EX_InstType(EX_InstType),
    .ID_InstType(ID_InstType), .Reset(in_1), .PauseIF(PauseIF), .PauseID(PauseID), .PauseEx(PauseEx),
    .PauseWB(PauseWB));
  IF_Ctrl if_ctrl_1 (.clk(clk1), .Pause(PauseIF), .IF_clk(IF_clk));
  ID_Ctrl id_ctrl_1 (.clk1(clk1), .clk2(clk2), .Pause(PauseID), .ID_clk1(ID_clk1), .ID_clk2(ID_clk2));
  Ex_Ctrl ex_ctrl_1 (.clk(clk1), .Pause(PauseEx), .Ex_clk(EX_clk));
  MEM_Ctrl mem_ctrl_1 (.clk(clk1), .Pause(PauseWB), .MEM_clk(MEM_clk));
  IF_Reg if_reg_1 (
    .clk(IF_clk), .Reset(in_1), .Inst(rom_1_data), .PC(programcounter_1_pc_out),
    .Inst_Out(if_reg_1_inst_out), .PC_Out(PC));
  InstDecoder instdecoder_1 (
    .Inst(if_reg_1_inst_out), .J_Addr(JInsttoPC), .I_Imm(InstImm), .Func(instdecoder_1_func), .Shamt(Shamt),
    .Rd(instdecoder_1_rd), .Rt(instdecoder_1_rt), .Rs(instdecoder_1_rs), .Op(instdecoder_1_op));
  CtrlUnit ctrlunit_1 (
    .OpCode(instdecoder_1_op), .Funct(instdecoder_1_func), .PCWr(PCWr), .PC_Branch(PC_Branch),
    .PC_Src(PC_Src), .W_En(W_En), .RegInstType(RegInstType), .JumpMode(JumpMode), .isUnsigned(isUnsigned),
    .ALUOp(ALUOp), .ALUSel(ALUSel), .BranchMode(BranchMode), .MemRd(MemRd), .MemWr(MemWr),
    .MemSMode(MemSMode), .MemLMode(MemLMode), .WBSel(WBSel));  // open: MF_SpReg, MF_Mode
  // Probe on W_Reg
  regSelUnit regselunit_1 (
    .RegInstType(RegInstType), .RegJumpMode(JumpMode), .Rd(instdecoder_1_rd), .Rt(instdecoder_1_rt),
    .Rs(instdecoder_1_rs), .W_Reg(W_Reg), .R_Reg1(regselunit_1_r_reg1), .R_Reg2(regselunit_1_r_reg2));
  // Probe on writebackunit_1_toreg
  or or_1 (or_1_out, MEM_clk, ID_clk1);
  // Probe on regselunit_1_r_reg1
  // Probe on regselunit_1_r_reg2
  // Probe on WRO
  // Probe on PC_Src
  // Probe on ALUOp
  // Probe on R_data2
  // Probe on R_data1
  register_group32 register_group32_1 (
    .clk(or_1_out), .W_En(WENO), .W_data(writebackunit_1_toreg), .W_Reg(WRO), .R_Reg1(regselunit_1_r_reg1),
    .R_Reg2(regselunit_1_r_reg2), .R_data1(R_data1), .R_data2(R_data2));
  // Probe on RDT2O
  ID_Reg id_reg_1 (
    .clk(ID_clk2), .Reset(in_1), .PC_Wr(PCWr), .PC_Branch(PC_Branch), .PC_Src(PC_Src), .JInsttoPC(JInsttoPC),
    .PC(PC), .R_Data1(R_data1), .R_Data2(R_data2), .isUnsigned(isUnsigned), .ALU_Op(ALUOp), .ALU_Sel(ALUSel),
    .BranchMode(BranchMode), .InstImm(InstImm), .Shamt(Shamt), .MemRd(MemRd), .MemWr(MemWr),
    .MemSMode(MemSMode), .MemLMode(MemLMode), .WBSel(WBSel), .W_En(W_En), .JumpMode(JumpMode),
    .RegInstType(RegInstType), .W_Reg(W_Reg), .PCWO(PCWO), .PCBO(PCBO), .PCSO(PCSO), .RTPO(RTPO),
    .IMTPO(IMTPO), .JITPO(JITPO), .PCO(PCO), .RDT1O(RDT1O), .RDT2O(RDT2O), .IUO(IUO), .ALUOPO(ALUOPO),
    .ALUSELO(ALUSELO), .BMO(BMO), .IIMO(IIMO), .SHAMTO(SHAMTO), .MRO(id_reg_1_mro), .MWO(id_reg_1_mwo),
    .MSMO(id_reg_1_msmo), .MLMO(id_reg_1_mlmo), .RTMO(id_reg_1_rtmo), .WBSO(id_reg_1_wbso),
    .WENO(id_reg_1_weno), .JMO(JMO), .RITO(ID_InstType), .WRO(id_reg_1_wro));
  Adder #(.width(16)) adder_1 (.a(PC), .b(16'h3004), .out(adder_1_out));  // open: cin, cout
  // Probe on id_reg_1_rtmo
  // Probe on aluselunit_1_opnuma
  ALUSelUnit aluselunit_1 (
    .ALUSel(ALUSELO), .PC(adder_1_out), .RegR1(RDT1O), .RegR2(RDT2O), .InstImm(IIMO), .Shamt(SHAMTO),
    .OpNumA(aluselunit_1_opnuma), .OpNumB(aluselunit_1_opnumb));
  // Probe on ALUResult1
  // Probe on ALUResult2
  alu_extend alu_extend_1 (
    .A32(aluselunit_1_opnuma), .B32(aluselunit_1_opnumb), .OP4(ALUOPO), .Result1(ALUResult1),
    .Result2(ALUResult2));
  // Probe on BMO
  // Probe on RTMO
  Ex_Reg ex_reg_1 (
    .clk(EX_clk), .Reset(in_1), .ALURes1(ALUResult1), .ALURes2(ALUResult2), .BranchtoPC(BranchtoPC),
    .MemRd(id_reg_1_mro), .MemWr(id_reg_1_mwo), .MemSMode(id_reg_1_msmo), .MemLMode(id_reg_1_mlmo),
    .RegtoMem(id_reg_1_rtmo), .WBSel(id_reg_1_wbso), .W_En(id_reg_1_weno), .JumpMode(JMO),
    .RegInstType(ID_InstType), .W_Reg(id_reg_1_wro), .ALUR1O(Ex_ALUR1O), .ALUR2O(Ex_ALUR2O), .BTPO(BTPO),
    .MRO(MRO), .MWO(MWO), .MSMO(MSMO), .MLMO(MLMO), .RTMO(RTMO), .WBSO(ex_reg_1_wbso), .WENO(ex_reg_1_weno),
    .JMO(ex_reg_1_jmo), .RITO(EX_InstType), .WRO(EX_WReg));
  // Probe on BranchtoPC
  BranchControlUnit branchcontrolunit_1 (.BranchMode(BMO), .ALU_Res1(ALUResult1), .BranchtoPC(BranchtoPC));
  MemoryControlUnit memorycontrolunit_1 (
    .clk(MEM_clk), .MemRd(MRO), .MemWr(MWO), .MemSMode(MSMO), .MemLMode(MLMO), .ALU_Res1(Ex_ALUR1O),
    .ALU_Res2(Ex_ALUR2O), .RegtoMem(RTMO), .MemOut(ram_1_dout), .Mem_Clk(memorycontrolunit_1_mem_clk),
    .MemRdEn(memorycontrolunit_1_memrden), .MemWrEn(memorycontrolunit_1_memwren),
    .Mem_Addr(memorycontrolunit_1_mem_addr), .MemW_data(memorycontrolunit_1_memw_data),
    .BE3(memorycontrolunit_1_be3), .BE2(memorycontrolunit_1_be2), .BE1(memorycontrolunit_1_be1),
    .BE0(memorycontrolunit_1_be0), .MemR_data(MemtoWB));
  // Probe on memorycontrolunit_1_mem_addr
  RAM #(.addrWidth(16), .byteenables("byteEnables"), .dataWidth(32)) ram_1 (
    .addr(memorycontrolunit_1_mem_addr), .we(memorycontrolunit_1_memwren), .oe(memorycontrolunit_1_memrden),
    .clk(memorycontrolunit_1_mem_clk), .din(memorycontrolunit_1_memw_data), .dout(ram_1_dout),
    .be3(memorycontrolunit_1_be3), .be2(memorycontrolunit_1_be2), .be1(memorycontrolunit_1_be1),
    .be0(memorycontrolunit_1_be0));
  // Probe on memorycontrolunit_1_memw_data
  // Probe on WB_ALUR1O
  MEM_Reg mem_reg_1 (
    .clk(MEM_clk), .Reset(in_1), .ALURes1(Ex_ALUR1O), .ALURes2(Ex_ALUR2O), .MemtoWB(MemtoWB),
    .WBSel(ex_reg_1_wbso), .W_En(ex_reg_1_weno), .JumpMode(ex_reg_1_jmo), .RegInstType(EX_InstType),
    .W_Reg(EX_WReg), .ALUR1O(WB_ALUR1O), .ALUR2O(WB_ALUR2O), .MTWBO(MTWBO), .WBSO(WBSO), .WENO(WENO),
    .WRO(WRO));  // open: JMO, RITO
  WriteBackUnit writebackunit_1 (
    .WBSel(WBSO), .ALU_Res1(WB_ALUR1O), .ALU_Res2(WB_ALUR2O), .Mem_data(MTWBO), .ToReg(writebackunit_1_toreg));

  // Other names for the same wires on the sheet: Reset = in_1

  // Notes on the sheet:
  //   contents of rom_1 (hex, n*v repeats v):
  //   200501ff ac050000 a4050006 a005000b 24050002 ac05000c a52820 ac050010 a52821 ac050014 a52822
  //   ac050018 20050040 20060020 a62823 ac05001c 20050003 52880 ac050020 52882 ac050024 20050005 20060002
  //   c52804 ac050028 c52806 ac05002c 20050007 52843 ac050030 20060001 c52807 ac050034 200501ff ac050038
  //   ac05003c 20050005 a52824 ac050040 30a50000 ac050044 20050005 20060002 a63825 ac070048 a63827
  //   ac07004c 34a70002 ac070050 a63826 ac070054 38a70002 ac070058 200501ff a405005e 8c05005c ac050060
  //   8405005e ac050064 8000c00
endmodule

module InstDecoder (
  input  [31:0] Inst,
  output [25:0] J_Addr,
  output [15:0] I_Imm,
  output [5:0] Func,
  output [4:0] Shamt,
  output [4:0] Rd,
  output [4:0] Rt,
  output [4:0] Rs,
  output [5:0] Op
);

  BitSelector #(.group(26), .width(32)) bitselector_1 (.in(Inst), .out(J_Addr), .sel(1'b0));
  BitSelector #(.group(16), .width(32)) bitselector_2 (.in(Inst), .out(I_Imm), .sel(1'b0));

  assign Func = Inst[5:0];
  assign Op = Inst[31:26];
  assign Rd = Inst[15:11];
  assign Rs = Inst[25:21];
  assign Rt = Inst[20:16];
  assign Shamt = Inst[10:6];
endmodule

module ProgramCounter (
  input  clk,
  input  PCWr,
  input  PC_Branch,
  input  [1:0] PC_JumpMode,
  input  [1:0] PC_Src,
  input  [1:0] BranchtoPC,
  input  [15:0] ImmtoPC,
  input  [25:0] JInsttoPC,
  input  [31:0] RegtoPC,
  output [15:0] PC_Out
);

  wire [1:0] multiplexer_2_out;
  wire [31:0] adder_1_out, adder_2_out, bit_extender_1_out, bit_extender_2_out, multiplexer_1_out,
       multiplexer_3_out, multiplexer_4_out, register_1_q, shifter_1_out, shifter_2_out, subtractor_1_out;

  assign bit_extender_1_out = {{16{1'b0}}, ImmtoPC};  // Bit_Extender bit_extender_1
  assign bit_extender_2_out = {{6{1'b0}}, JInsttoPC};  // Bit_Extender bit_extender_2
  Shifter #(.width(32)) shifter_1 (.in(bit_extender_1_out), .\dist (5'b00010), .out(shifter_1_out));
  Shifter #(.width(32)) shifter_2 (.in(bit_extender_2_out), .\dist (5'b00010), .out(shifter_2_out));
  Adder #(.width(32)) adder_1 (.a(32'h4), .b(shifter_1_out), .out(adder_1_out));  // open: cin, cout
  Multiplexer #(.select(2), .width(32)) multiplexer_1 (
    .in0(shifter_2_out), .in1(shifter_2_out), .in2(RegtoPC), .in3(RegtoPC), .out(multiplexer_1_out),
    .sel(PC_JumpMode));
  Subtractor #(.width(32)) subtractor_1 (
    .a(multiplexer_1_out), .b(32'h3000), .out(subtractor_1_out));  // open: bin, bout
  Multiplexer #(.width(2)) multiplexer_2 (.in0(PC_Src), .in1(BranchtoPC), .out(multiplexer_2_out), .sel(PC_Branch));
  Multiplexer #(.select(2), .width(32)) multiplexer_3 (
    .in0(32'h3000), .in1(adder_2_out), .in2(adder_2_out), .in3(subtractor_1_out), .out(multiplexer_3_out),
    .sel(multiplexer_2_out));
  Register #(.width(32)) register_1 (.D(multiplexer_3_out), .en(PCWr), .clk(clk), .Q(register_1_q));  // open: clr
  Multiplexer #(.select(2), .width(32)) multiplexer_4 (
    .in0({32{1'b0}}), .in1(32'h4), .in2(adder_1_out), .in3({32{1'b0}}), .out(multiplexer_4_out),
    .sel(multiplexer_2_out));
  BitSelector #(.group(16), .width(32)) bitselector_1 (.in(register_1_q), .out(PC_Out), .sel(1'b0));
  Adder #(.width(32)) adder_2 (.a(register_1_q), .b(multiplexer_4_out), .out(adder_2_out));  // open: cin, cout
endmodule

module CtrlUnit (
  input  [5:0] OpCode,
  input  [5:0] Funct,
  output PCWr,
  output PC_Branch,
  output [1:0] PC_Src,
  output W_En,
  output [1:0] RegInstType,
  output [1:0] JumpMode,
  output isUnsigned,
  output [3:0] ALUOp,
  output [3:0] ALUSel,
  output [1:0] BranchMode,
  output MemRd,
  output MemWr,
  output [1:0] MemSMode,
  output [2:0] MemLMode,
  output [1:0] WBSel,
  output MF_SpReg,
  output MF_Mode
);

  wire algctrlunit_1_isunsigned, algctrlunit_1_memrd, algctrlunit_1_memwr, algctrlunit_1_pc_branch,
       algctrlunit_1_pcwr, algctrlunit_1_w_en, comparator_1_eq, datapathctrlunit_1_isunsigned,
       datapathctrlunit_1_memrd, datapathctrlunit_1_memwr, datapathctrlunit_1_pc_branch,
       datapathctrlunit_1_pcwr, datapathctrlunit_1_w_en;
  wire [1:0] algctrlunit_1_branchmode, algctrlunit_1_jumpmode, algctrlunit_1_memsmode, algctrlunit_1_pc_src,
       algctrlunit_1_reginsttype, algctrlunit_1_wbsel, datapathctrlunit_1_branchmode,
       datapathctrlunit_1_jumpmode, datapathctrlunit_1_memsmode, datapathctrlunit_1_pc_src,
       datapathctrlunit_1_reginsttype, datapathctrlunit_1_wbsel;
  wire [2:0] algctrlunit_1_memlmode, datapathctrlunit_1_memlmode;
  wire [3:0] algctrlunit_1_aluop, algctrlunit_1_alusel, datapathctrlunit_1_aluop, datapathctrlunit_1_alusel;

  Comparator #(.width(6)) comparator_1 (.a(OpCode), .b({6{1'b0}}), .eq(comparator_1_eq));  // open: gt, lt
  DatapathCtrlUnit datapathctrlunit_1 (
    .OpCode(OpCode), .PCWr(datapathctrlunit_1_pcwr), .PC_Branch(datapathctrlunit_1_pc_branch),
    .PC_Src(datapathctrlunit_1_pc_src), .W_En(datapathctrlunit_1_w_en),
    .RegInstType(datapathctrlunit_1_reginsttype), .JumpMode(datapathctrlunit_1_jumpmode),
    .isUnsigned(datapathctrlunit_1_isunsigned), .ALUOp(datapathctrlunit_1_aluop),
    .ALUSel(datapathctrlunit_1_alusel), .BranchMode(datapathctrlunit_1_branchmode),
    .MemRd(datapathctrlunit_1_memrd), .MemWr(datapathctrlunit_1_memwr),
    .MemSMode(datapathctrlunit_1_memsmode), .MemLMode(datapathctrlunit_1_memlmode),
    .WBSel(datapathctrlunit_1_wbsel));
  AlgCtrlUnit algctrlunit_1 (
    .OpCode(Funct), .PCWr(algctrlunit_1_pcwr), .PC_Branch(algctrlunit_1_pc_branch),
    .PC_Src(algctrlunit_1_pc_src), .W_En(algctrlunit_1_w_en), .RegInstType(algctrlunit_1_reginsttype),
    .JumpMode(algctrlunit_1_jumpmode), .isUnsigned(algctrlunit_1_isunsigned), .ALUOp(algctrlunit_1_aluop),
    .ALUSel(algctrlunit_1_alusel), .BranchMode(algctrlunit_1_branchmode), .MemRd(algctrlunit_1_memrd),
    .MemWr(algctrlunit_1_memwr), .MemSMode(algctrlunit_1_memsmode), .MemLMode(algctrlunit_1_memlmode),
    .WBSel(algctrlunit_1_wbsel));
  Multiplexer multiplexer_1 (
    .in0(datapathctrlunit_1_pcwr), .in1(algctrlunit_1_pcwr), .out(PCWr), .sel(comparator_1_eq));
  Multiplexer multiplexer_2 (
    .in0(datapathctrlunit_1_pc_branch), .in1(algctrlunit_1_pc_branch), .out(PC_Branch), .sel(comparator_1_eq));
  Multiplexer #(.width(2)) multiplexer_3 (
    .in0(datapathctrlunit_1_pc_src), .in1(algctrlunit_1_pc_src), .out(PC_Src), .sel(comparator_1_eq));
  Multiplexer multiplexer_4 (
    .in0(datapathctrlunit_1_w_en), .in1(algctrlunit_1_w_en), .out(W_En), .sel(comparator_1_eq));
  Multiplexer #(.width(2)) multiplexer_5 (
    .in0(datapathctrlunit_1_reginsttype), .in1(algctrlunit_1_reginsttype), .out(RegInstType),
    .sel(comparator_1_eq));
  Multiplexer #(.width(2)) multiplexer_6 (
    .in0(datapathctrlunit_1_jumpmode), .in1(algctrlunit_1_jumpmode), .out(JumpMode), .sel(comparator_1_eq));
  Multiplexer multiplexer_7 (
    .in0(datapathctrlunit_1_isunsigned), .in1(algctrlunit_1_isunsigned), .out(isUnsigned),
    .sel(comparator_1_eq));
  Multiplexer #(.width(4)) multiplexer_8 (
    .in0(datapathctrlunit_1_aluop), .in1(algctrlunit_1_aluop), .out(ALUOp), .sel(comparator_1_eq));
  Multiplexer #(.width(4)) multiplexer_9 (
    .in0(datapathctrlunit_1_alusel), .in1(algctrlunit_1_alusel), .out(ALUSel), .sel(comparator_1_eq));
  Multiplexer #(.width(2)) multiplexer_10 (
    .in0(datapathctrlunit_1_branchmode), .in1(algctrlunit_1_branchmode), .out(BranchMode),
    .sel(comparator_1_eq));
  Multiplexer multiplexer_11 (
    .in0(datapathctrlunit_1_memrd), .in1(algctrlunit_1_memrd), .out(MemRd), .sel(comparator_1_eq));
  Multiplexer multiplexer_12 (
    .in0(datapathctrlunit_1_memwr), .in1(algctrlunit_1_memwr), .out(MemWr), .sel(comparator_1_eq));
  Multiplexer #(.width(2)) multiplexer_13 (
    .in0(datapathctrlunit_1_memsmode), .in1(algctrlunit_1_memsmode), .out(MemSMode), .sel(comparator_1_eq));
  Multiplexer #(.width(3)) multiplexer_14 (
    .in0(datapathctrlunit_1_memlmode), .in1(algctrlunit_1_memlmode), .out(MemLMode), .sel(comparator_1_eq));
  Multiplexer #(.width(2)) multiplexer_15 (
    .in0(datapathctrlunit_1_wbsel), .in1(algctrlunit_1_wbsel), .out(WBSel), .sel(comparator_1_eq));
endmodule

module DatapathCtrlUnit (
  input  [5:0] OpCode,
  output PCWr,
  output PC_Branch,
  output [1:0] PC_Src,
  output W_En,
  output [1:0] RegInstType,
  output [1:0] JumpMode,
  output isUnsigned,
  output [3:0] ALUOp,
  output [3:0] ALUSel,
  output [1:0] BranchMode,
  output MemRd,
  output MemWr,
  output [1:0] MemSMode,
  output [2:0] MemLMode,
  output [1:0] WBSel
);

  wire and_3_out, and_4_out, and_5_out, and_8_out, and_9_out, and_10_out, and_11_out, and_12_out, and_13_out,
       and_14_out, and_15_out, and_16_out, and_17_out, and_18_out, and_19_out, and_21_out, and_22_out,
       not_1_out, not_2_out, not_3_out, not_4_out, not_5_out;

  not not_1 (not_1_out, OpCode[5]);
  not not_2 (not_2_out, OpCode[3]);
  not not_3 (not_3_out, OpCode[2]);
  not not_4 (not_4_out, OpCode[1]);
  not not_5 (not_5_out, OpCode[0]);
  and and_1 (PC_Branch, not_1_out, not_2_out, OpCode[2]);
  and and_2 (PC_Src[1], not_1_out, not_2_out, not_3_out);
  or or_1 (PC_Src[0], not_3_out, OpCode[5], OpCode[3]);
  and and_3 (and_3_out, OpCode[5], not_2_out);
  and and_4 (and_4_out, not_1_out, OpCode[3]);
  and and_5 (and_5_out, not_2_out, not_3_out, OpCode[0]);
  and and_6 (RegInstType[1], not_1_out, not_2_out, not_3_out);
  or or_2 (RegInstType[0], OpCode[5], OpCode[2], not_4_out);
  and and_7 (JumpMode[0], not_1_out, not_2_out, not_3_out, OpCode[0]);
  and and_8 (and_8_out, OpCode[5], OpCode[2]);
  and and_9 (and_9_out, not_1_out, not_3_out, not_4_out, OpCode[0]);
  and and_10 (and_10_out, OpCode[3], OpCode[2], OpCode[0]);
  and and_11 (and_11_out, OpCode[3], OpCode[1], not_5_out);
  and and_12 (and_12_out, not_2_out, OpCode[2]);
  and and_13 (and_13_out, not_4_out, not_5_out);
  and and_14 (and_14_out, not_3_out, OpCode[0]);
  and and_15 (and_15_out, not_1_out, not_2_out, not_4_out);
  and and_16 (and_16_out, not_1_out, OpCode[2], not_4_out, not_5_out);
  and and_17 (and_17_out, OpCode[2], OpCode[1]);
  and and_18 (and_18_out, OpCode[3], not_5_out);
  and and_19 (and_19_out, not_3_out, OpCode[0]);
  and and_20 (ALUSel[2], not_1_out, not_2_out, not_3_out, OpCode[0]);
  and and_21 (and_21_out, not_2_out, OpCode[2], OpCode[1]);
  and and_22 (and_22_out, not_1_out, not_2_out, not_3_out, OpCode[0]);
  or or_3 (ALUSel[0], OpCode[5], OpCode[3]);
  and and_23 (BranchMode[1], not_2_out, OpCode[2], OpCode[1]);
  and and_24 (BranchMode[0], not_1_out, not_2_out, OpCode[2], OpCode[0]);
  and and_25 (MemRd, OpCode[5], not_2_out);
  and and_26 (MemWr, OpCode[5], OpCode[3]);
  and and_27 (MemSMode[1], OpCode[3], not_3_out, OpCode[1]);
  and and_28 (MemSMode[0], OpCode[5], OpCode[3], not_4_out, OpCode[0]);
  and and_29 (MemLMode[2], OpCode[5], not_2_out, OpCode[1]);
  and and_30 (MemLMode[1], OpCode[5], not_2_out, not_4_out, OpCode[0]);
  and and_31 (MemLMode[0], OpCode[5], OpCode[2]);
  or or_4 (W_En, and_3_out, and_4_out, and_5_out);
  or or_5 (isUnsigned, and_8_out, and_9_out);
  or or_6 (ALUOp[3], and_10_out, and_11_out);
  or or_7 (ALUOp[2], and_12_out, and_13_out, and_14_out);
  or or_8 (ALUOp[1], and_15_out, and_16_out);
  or or_9 (ALUOp[0], OpCode[5], and_17_out, and_18_out, and_19_out);
  or or_10 (ALUSel[1], and_21_out, and_22_out);

  assign ALUSel[3] = 1'b0;
  assign JumpMode[1] = 1'b0;
  assign PCWr = 1'b1;
  assign WBSel = {1'b0, OpCode[5]};
endmodule

module AlgCtrlUnit (
  input  [5:0] OpCode,
  output PCWr,
  output PC_Branch,
  output [1:0] PC_Src,
  output W_En,
  output [1:0] RegInstType,
  output [1:0] JumpMode,
  output isUnsigned,
  output [3:0] ALUOp,
  output [3:0] ALUSel,
  output [1:0] BranchMode,
  output MemRd,
  output MemWr,
  output [1:0] MemSMode,
  output [2:0] MemLMode,
  output [1:0] WBSel
);

  wire and_6_out, and_7_out, and_8_out, and_9_out, and_10_out, and_11_out, and_12_out, and_13_out,
       and_14_out, and_15_out, and_16_out, and_17_out, and_18_out, and_19_out, and_20_out, and_21_out,
       and_22_out, and_24_out, and_25_out, not_1_out, not_2_out, not_3_out, not_4_out, not_5_out, not_6_out;

  not not_1 (not_1_out, OpCode[5]);
  not not_2 (not_2_out, OpCode[4]);
  not not_3 (not_3_out, OpCode[3]);
  not not_4 (not_4_out, OpCode[2]);
  not not_5 (not_5_out, OpCode[1]);
  not not_6 (not_6_out, OpCode[0]);
  and and_1 (PC_Src[1], not_2_out, OpCode[3]);
  or or_1 (W_En, not_3_out, OpCode[0], OpCode[4]);
  and and_2 (RegInstType[1], not_2_out, OpCode[3]);
  and and_3 (RegInstType[0], not_1_out, not_3_out);
  and and_4 (JumpMode[1], not_2_out, OpCode[3]);
  and and_5 (JumpMode[0], not_1_out, not_2_out, not_5_out, OpCode[0]);
  and and_6 (and_6_out, OpCode[5], not_4_out, OpCode[0]);
  and and_7 (and_7_out, OpCode[4], OpCode[0]);
  and and_8 (and_8_out, OpCode[5], OpCode[2], OpCode[1]);
  and and_9 (and_9_out, OpCode[2], not_5_out, OpCode[0]);
  and and_10 (and_10_out, OpCode[5], not_4_out);
  and and_11 (and_11_out, OpCode[5], not_5_out, not_6_out);
  and and_12 (and_12_out, not_2_out, not_4_out, not_5_out, OpCode[0]);
  and and_13 (and_13_out, OpCode[3], OpCode[1]);
  and and_14 (and_14_out, OpCode[5], OpCode[2], not_5_out, not_6_out);
  and and_15 (and_15_out, OpCode[5], OpCode[1], OpCode[0]);
  and and_16 (and_16_out, OpCode[4], not_5_out);
  and and_17 (and_17_out, not_3_out, not_4_out, OpCode[1], not_6_out);
  and and_18 (and_18_out, not_1_out, not_3_out, OpCode[1], not_6_out);
  and and_19 (and_19_out, OpCode[5], OpCode[2], not_6_out);
  and and_20 (and_20_out, OpCode[4], not_5_out);
  and and_21 (and_21_out, OpCode[5], not_4_out, not_5_out);
  and and_22 (and_22_out, not_1_out, not_2_out, OpCode[0]);
  and and_23 (ALUSel[3], not_1_out, not_3_out, not_4_out);
  and and_24 (and_24_out, not_1_out, not_3_out, not_4_out);
  and and_25 (and_25_out, not_1_out, not_2_out, not_4_out, OpCode[0]);
  and and_26 (ALUSel[1], not_1_out, not_2_out, not_5_out, OpCode[0]);
  or or_2 (isUnsigned, and_6_out, and_7_out);
  or or_3 (ALUOp[3], and_8_out, and_9_out);
  or or_4 (ALUOp[2], and_10_out, and_11_out, and_12_out, and_13_out);
  or or_5 (ALUOp[1], and_14_out, and_15_out, and_16_out, and_17_out, and_18_out);
  or or_6 (ALUOp[0], and_19_out, and_20_out, and_21_out, and_22_out);
  or or_7 (ALUSel[2], and_24_out, and_25_out);

  assign ALUSel[0] = 1'b0;
  assign BranchMode = 2'b00;
  assign MemLMode = 3'b000;
  assign MemRd = 1'b0;
  assign MemSMode = 2'b00;
  assign MemWr = 1'b0;
  assign PC_Branch = 1'b0;
  assign PC_Src[0] = 1'b1;
  assign PCWr = 1'b1;
  assign WBSel = 2'b00;
endmodule

module test (
  input  in_1,
  input  in_2
);

  wire [31:0] ram_1_dout;

  RAM #(.addrWidth(16), .byteenables("byteEnables"), .dataWidth(32)) ram_1 (
    .addr(16'h1), .we(in_2), .clk(in_1), .din(32'h1ff), .dout(ram_1_dout), .be3(in_1), .be2(in_1),
    .be1(in_1), .be0(in_1));  // open: oe
  // Probe on ram_1_dout
endmodule

module WriteBackUnit (
  input  [1:0] WBSel,
  input  [31:0] ALU_Res1,
  input  [31:0] ALU_Res2,
  input  [31:0] Mem_data,
  output [31:0] ToReg
);

  Multiplexer #(.select(2), .width(32)) multiplexer_1 (
    .in0(ALU_Res1), .in1(Mem_data), .out(ToReg), .sel(WBSel));  // open: in2, in3
endmodule

module MemoryControlUnit (
  input  clk,
  input  MemRd,
  input  MemWr,
  input  [1:0] MemSMode,
  input  [2:0] MemLMode,
  input  [31:0] ALU_Res1,
  input  [31:0] ALU_Res2,
  input  [31:0] RegtoMem,
  input  [31:0] MemOut,
  output Mem_Clk,
  output MemRdEn,
  output MemWrEn,
  output [15:0] Mem_Addr,
  output [31:0] MemW_data,
  output BE3,
  output BE2,
  output BE1,
  output BE0,
  output [31:0] MemR_data
);

  wire ldworddecoder_1_be0, ldworddecoder_1_be1, ldworddecoder_1_be2, ldworddecoder_1_be3, not_1_out,
       savworddecoder_1_be0, savworddecoder_1_be1, savworddecoder_1_be2, savworddecoder_1_be3;
  wire [1:0] bitselector_1_out;
  wire [4:0] multiplexer_1_out;
  wire [7:0] bitselector_2_out, bitselector_3_out;
  wire [15:0] bitselector_4_out, bitselector_5_out;
  wire [31:0] bit_extender_1_out, bit_extender_2_out, bit_extender_3_out, bit_extender_4_out, shifter_1_out,
       shifter_2_out;

  Shifter #(.shift("lr"), .width(32)) shifter_1 (.in(ALU_Res1), .\dist (5'b00010), .out(shifter_1_out));
  BitSelector #(.group(2), .width(32)) bitselector_1 (.in(ALU_Res1), .out(bitselector_1_out), .sel(4'b0000));
  Multiplexer #(.select(2), .width(5)) multiplexer_1 (
    .in0({5{1'b0}}), .in1(5'b01000), .in2(5'b10000), .in3(5'b11000), .out(multiplexer_1_out),
    .sel(bitselector_1_out));
  Shifter #(.shift("lr"), .width(32)) shifter_2 (.in(MemOut), .\dist (multiplexer_1_out), .out(shifter_2_out));
  Shifter #(.width(32)) shifter_3 (.in(RegtoMem), .\dist (multiplexer_1_out), .out(MemW_data));
  BitSelector #(.group(8), .width(32)) bitselector_2 (.in(shifter_2_out), .out(bitselector_2_out), .sel(2'b00));
  BitSelector #(.group(8), .width(32)) bitselector_3 (.in(shifter_2_out), .out(bitselector_3_out), .sel(2'b00));
  BitSelector #(.group(16), .width(32)) bitselector_4 (.in(shifter_2_out), .out(bitselector_4_out), .sel(1'b0));
  BitSelector #(.group(16), .width(32)) bitselector_5 (.in(shifter_2_out), .out(bitselector_5_out), .sel(1'b0));
  BitSelector #(.group(16), .width(32)) bitselector_6 (.in(shifter_1_out), .out(Mem_Addr), .sel(1'b0));
  assign bit_extender_1_out = {{24{bitselector_2_out[7]}}, bitselector_2_out};  // Bit_Extender bit_extender_1
  assign bit_extender_2_out = {{24{1'b0}}, bitselector_3_out};  // Bit_Extender bit_extender_2
  assign bit_extender_3_out = {{16{bitselector_4_out[15]}}, bitselector_4_out};  // Bit_Extender bit_extender_3
  assign bit_extender_4_out = {{16{1'b0}}, bitselector_5_out};  // Bit_Extender bit_extender_4
  not not_1 (not_1_out, MemWr);
  Multiplexer #(.select(3), .width(32)) multiplexer_2 (
    .in0(bit_extender_1_out), .in1(bit_extender_2_out), .in2(bit_extender_3_out), .in3(bit_extender_4_out),
    .in4(shifter_2_out), .out(MemR_data), .sel(MemLMode));  // open: in5, in6, in7
  SavWordDecoder savworddecoder_1 (
    .MemSMode(MemSMode), .Offset(bitselector_1_out), .BE3(savworddecoder_1_be3), .BE2(savworddecoder_1_be2),
    .BE1(savworddecoder_1_be1), .BE0(savworddecoder_1_be0));
  LdWordDecoder ldworddecoder_1 (
    .MemLMode(MemLMode), .Offset(bitselector_1_out), .BE3(ldworddecoder_1_be3), .BE2(ldworddecoder_1_be2),
    .BE1(ldworddecoder_1_be1), .BE0(ldworddecoder_1_be0));
  Multiplexer multiplexer_3 (.in0(savworddecoder_1_be3), .in1(ldworddecoder_1_be3), .out(BE3), .sel(not_1_out));
  Multiplexer multiplexer_4 (.in0(savworddecoder_1_be2), .in1(ldworddecoder_1_be2), .out(BE2), .sel(not_1_out));
  Multiplexer multiplexer_5 (.in0(savworddecoder_1_be1), .in1(ldworddecoder_1_be1), .out(BE1), .sel(not_1_out));
  Multiplexer multiplexer_6 (.in0(savworddecoder_1_be0), .in1(ldworddecoder_1_be0), .out(BE0), .sel(not_1_out));

  assign Mem_Clk = clk;
  assign MemRdEn = MemRd;
  assign MemWrEn = MemWr;
endmodule

module ALUSelUnit (
  input  [3:0] ALUSel,
  input  [15:0] PC,
  input  [31:0] RegR1,
  input  [31:0] RegR2,
  input  [15:0] InstImm,
  input  [4:0] Shamt,
  output [31:0] OpNumA,
  output [31:0] OpNumB
);

  wire [31:0] bit_extender_1_out, bit_extender_2_out, bit_extender_3_out;

  assign bit_extender_1_out = {{16{1'b0}}, PC};  // Bit_Extender bit_extender_1
  assign bit_extender_2_out = {{16{1'b0}}, InstImm};  // Bit_Extender bit_extender_2
  assign bit_extender_3_out = {{27{1'b0}}, Shamt};  // Bit_Extender bit_extender_3
  Multiplexer #(.select(2), .width(32)) multiplexer_1 (
    .in0(RegR1), .in1(bit_extender_1_out), .in2({32{1'b0}}), .in3(bit_extender_3_out), .out(OpNumA),
    .sel(ALUSel[3:2]));
  Multiplexer #(.select(2), .width(32)) multiplexer_2 (
    .in0(RegR2), .in1(bit_extender_2_out), .in2({32{1'b0}}), .out(OpNumB), .sel(ALUSel[1:0]));  // open: in3
endmodule

module BranchControlUnit (
  input  [1:0] BranchMode,
  input  [31:0] ALU_Res1,
  output [1:0] BranchtoPC
);

  wire comparator_1_eq, comparator_2_eq, comparator_2_gt, comparator_2_lt, multiplexer_1_out, not_1_out,
       or_1_out;

  Comparator #(.mode("unsigned"), .width(32)) comparator_1 (
    .a(ALU_Res1), .b({32{1'b0}}), .eq(comparator_1_eq));  // open: gt, lt
  Comparator #(.mode("unsigned"), .width(32)) comparator_2 (
    .a(ALU_Res1), .b({32{1'b0}}), .gt(comparator_2_gt), .eq(comparator_2_eq), .lt(comparator_2_lt));
  not not_1 (not_1_out, comparator_1_eq);
  or or_1 (or_1_out, comparator_2_eq, comparator_2_lt);
  Multiplexer #(.select(2)) multiplexer_1 (
    .in0(comparator_1_eq), .in1(not_1_out), .in2(or_1_out), .in3(comparator_2_gt), .out(multiplexer_1_out),
    .sel(BranchMode));
  Multiplexer #(.width(2)) multiplexer_2 (.in0(2'b01), .in1(2'b10), .out(BranchtoPC), .sel(multiplexer_1_out));
endmodule

module regSelUnit (
  input  [1:0] RegInstType,
  input  [1:0] RegJumpMode,
  input  [4:0] Rd,
  input  [4:0] Rt,
  input  [4:0] Rs,
  output [4:0] W_Reg,
  output [4:0] R_Reg1,
  output [4:0] R_Reg2
);

  wire [4:0] multiplexer_1_out, multiplexer_2_out;

  Multiplexer #(.select(2), .width(5)) multiplexer_1 (
    .in1({5{1'b1}}), .in3({5{1'b1}}), .out(multiplexer_1_out), .sel(RegJumpMode));  // open: in0, in2
  Multiplexer #(.select(2), .width(5)) multiplexer_2 (
    .in2(Rs), .in3(Rs), .out(multiplexer_2_out), .sel(RegJumpMode));  // open: in0, in1
  Multiplexer #(.select(2), .width(5)) multiplexer_3 (
    .in0(Rd), .in1(Rt), .in2(multiplexer_1_out), .in3(Rd), .out(W_Reg), .sel(RegInstType));
  Multiplexer #(.select(2), .width(5)) multiplexer_4 (
    .in0(Rs), .in1(Rs), .in2(multiplexer_2_out), .in3(Rs), .out(R_Reg1), .sel(RegInstType));
  Multiplexer #(.select(2), .width(5)) multiplexer_5 (
    .in0(Rt), .in1(Rt), .in3(Rt), .out(R_Reg2), .sel(RegInstType));  // open: in2
endmodule

module ClkUnit (
  input  Reset,
  input  EnClk,
  input  AM_Switch,
  input  Manual_Step,
  output clk1,
  output clk2,
  output clk3,
  output clk4,
  output clk5
);

  wire clock_1_out, multiplexer_1_out;
  wire [2:0] counter_1_q;

  Clock clock_1 (.out(clock_1_out));
  Multiplexer multiplexer_1 (.in0(clock_1_out), .in1(Manual_Step), .out(multiplexer_1_out), .sel(AM_Switch));
  Counter #(.max('h4), .width(3)) counter_1 (
    .clr(Reset), .up(1'b1), .count(EnClk), .clk(multiplexer_1_out), .Q(counter_1_q));  // open: load, D, carry
  Demultiplexer #(.select(3)) demultiplexer_1 (
    .out0(clk1), .out1(clk2), .out2(clk3), .out3(clk4), .out4(clk5), .in(1'b1), .sel(counter_1_q));  // open: out5, out6, out7
endmodule

module SavWordDecoder (
  input  [1:0] MemSMode,
  input  [1:0] Offset,
  output BE3,
  output BE2,
  output BE1,
  output BE0
);

  wire and_1_out, and_2_out, and_3_out, and_4_out, and_5_out, not_1_out, not_2_out;

  not not_1 (not_1_out, Offset[1]);
  not not_2 (not_2_out, Offset[0]);
  and and_1 (and_1_out, Offset[1], Offset[0]);
  and and_2 (and_2_out, MemSMode[0], Offset[1]);
  and and_3 (and_3_out, Offset[1], not_2_out);
  and and_4 (and_4_out, not_1_out, Offset[0]);
  and and_5 (and_5_out, MemSMode[0], not_1_out);
  and and_6 (BE0, not_1_out, not_2_out);
  or or_1 (BE3, and_1_out, and_2_out, MemSMode[1]);
  or or_2 (BE2, and_3_out, MemSMode[1]);
  or or_3 (BE1, and_4_out, and_5_out, MemSMode[1]);
endmodule

module LdWordDecoder (
  input  [2:0] MemLMode,
  input  [1:0] Offset,
  output BE3,
  output BE2,
  output BE1,
  output BE0
);

  wire and_1_out, and_2_out, and_3_out, and_4_out, and_5_out, not_1_out, not_2_out;

  not not_1 (not_1_out, Offset[1]);
  not not_2 (not_2_out, Offset[0]);
  and and_1 (and_1_out, Offset[1], Offset[0]);
  and and_2 (and_2_out, MemLMode[1], Offset[1]);
  and and_3 (and_3_out, Offset[1], not_2_out);
  and and_4 (and_4_out, not_1_out, Offset[0]);
  and and_5 (and_5_out, MemLMode[1], not_1_out);
  and and_6 (BE0, not_1_out, not_2_out);
  or or_1 (BE3, MemLMode[2], and_1_out, and_2_out);
  or or_2 (BE2, MemLMode[2], and_3_out);
  or or_3 (BE1, MemLMode[2], and_4_out, and_5_out);
endmodule

module IF_Reg (
  input  clk,
  input  Reset,
  input  [31:0] Inst,
  input  [15:0] PC,
  output [31:0] Inst_Out,
  output [15:0] PC_Out
);

  Register #(.width(32)) register_1 (.D(Inst), .en(1'b1), .clk(clk), .Q(Inst_Out), .clr(Reset));
  Register #(.width(16)) register_2 (.D(PC), .en(1'b1), .clk(clk), .Q(PC_Out), .clr(Reset));
endmodule

module ID_Reg (
  input  clk,
  input  Reset,
  input  PC_Wr,
  input  PC_Branch,
  input  [1:0] PC_Src,
  input  [25:0] JInsttoPC,
  input  [15:0] PC,
  input  [31:0] R_Data1,
  input  [31:0] R_Data2,
  input  isUnsigned,
  input  [3:0] ALU_Op,
  input  [3:0] ALU_Sel,
  input  [1:0] BranchMode,
  input  [15:0] InstImm,
  input  [4:0] Shamt,
  input  MemRd,
  input  MemWr,
  input  [1:0] MemSMode,
  input  [2:0] MemLMode,
  input  [1:0] WBSel,
  input  W_En,
  input  [1:0] JumpMode,
  input  [1:0] RegInstType,
  input  [4:0] W_Reg,
  output PCWO,
  output PCBO,
  output [1:0] PCSO,
  output [31:0] RTPO,
  output [15:0] IMTPO,
  output [25:0] JITPO,
  output [15:0] PCO,
  output [31:0] RDT1O,
  output [31:0] RDT2O,
  output IUO,
  output [3:0] ALUOPO,
  output [3:0] ALUSELO,
  output [1:0] BMO,
  output [15:0] IIMO,
  output [4:0] SHAMTO,
  output MRO,
  output MWO,
  output [1:0] MSMO,
  output [2:0] MLMO,
  output [31:0] RTMO,
  output [1:0] WBSO,
  output WENO,
  output [1:0] JMO,
  output [1:0] RITO,
  output [4:0] WRO
);

  Register #(.width(1)) register_1 (.D(PC_Wr), .en(1'b1), .clk(clk), .Q(PCWO), .clr(Reset));
  Register #(.width(1)) register_2 (.D(PC_Branch), .en(1'b1), .clk(clk), .Q(PCBO), .clr(Reset));
  Register #(.width(2)) register_3 (.D(PC_Src), .en(1'b1), .clk(clk), .Q(PCSO), .clr(Reset));
  Register #(.width(26)) register_4 (.D(JInsttoPC), .en(1'b1), .clk(clk), .Q(JITPO));  // open: clr
  Register #(.width(16)) register_5 (.D(PC), .en(1'b1), .clk(clk), .Q(PCO), .clr(Reset));
  Register #(.width(32)) register_6 (.D(R_Data1), .en(1'b1), .clk(clk), .Q(RDT1O), .clr(Reset));
  Register #(.width(32)) register_7 (.D(R_Data2), .en(1'b1), .clk(clk), .Q(RDT2O), .clr(Reset));
  Register #(.width(1)) register_8 (.D(isUnsigned), .en(1'b1), .clk(clk), .Q(IUO), .clr(Reset));
  Register #(.width(4)) register_9 (.D(ALU_Op), .en(1'b1), .clk(clk), .Q(ALUOPO), .clr(Reset));
  Register #(.width(4)) register_10 (.D(ALU_Sel), .en(1'b1), .clk(clk), .Q(ALUSELO), .clr(Reset));
  Register #(.width(2)) register_11 (.D(BranchMode), .en(1'b1), .clk(clk), .Q(BMO), .clr(Reset));
  Register #(.width(16)) register_12 (.D(InstImm), .en(1'b1), .clk(clk), .Q(IIMO), .clr(Reset));
  Register #(.width(5)) register_13 (.D(Shamt), .en(1'b1), .clk(clk), .Q(SHAMTO), .clr(Reset));
  Register #(.width(1)) register_14 (.D(MemRd), .en(1'b1), .clk(clk), .Q(MRO), .clr(Reset));
  Register #(.width(1)) register_15 (.D(MemWr), .en(1'b1), .clk(clk), .Q(MWO), .clr(Reset));
  Register #(.width(2)) register_16 (.D(MemSMode), .en(1'b1), .clk(clk), .Q(MSMO), .clr(Reset));
  Register #(.width(3)) register_17 (.D(MemLMode), .en(1'b1), .clk(clk), .Q(MLMO), .clr(Reset));
  Register #(.width(2)) register_18 (.D(WBSel), .en(1'b1), .clk(clk), .Q(WBSO), .clr(Reset));
  Register #(.width(1)) register_19 (.D(W_En), .en(1'b1), .clk(clk), .Q(WENO), .clr(Reset));
  Register #(.width(2)) register_20 (.D(JumpMode), .en(1'b1), .clk(clk), .Q(JMO), .clr(Reset));
  Register #(.width(2)) register_21 (.D(RegInstType), .en(1'b1), .clk(clk), .Q(RITO), .clr(Reset));
  Register #(.width(5)) register_22 (.D(W_Reg), .en(1'b1), .clk(clk), .Q(WRO), .clr(Reset));

  assign IMTPO = IIMO;
  assign RTMO = RDT2O;
  assign RTPO = RDT1O;
endmodule

module Ex_Reg (
  input  clk,
  input  Reset,
  input  [31:0] ALURes1,
  input  [31:0] ALURes2,
  input  [1:0] BranchtoPC,
  input  MemRd,
  input  MemWr,
  input  [1:0] MemSMode,
  input  [2:0] MemLMode,
  input  [31:0] RegtoMem,
  input  [1:0] WBSel,
  input  W_En,
  input  [1:0] JumpMode,
  input  [1:0] RegInstType,
  input  [4:0] W_Reg,
  output [31:0] ALUR1O,
  output [31:0] ALUR2O,
  output [1:0] BTPO,
  output MRO,
  output MWO,
  output [1:0] MSMO,
  output [2:0] MLMO,
  output [31:0] RTMO,
  output [1:0] WBSO,
  output WENO,
  output [1:0] JMO,
  output [1:0] RITO,
  output [4:0] WRO
);

  Register #(.width(32)) register_1 (.D(ALURes1), .en(clk), .clk(clk), .Q(ALUR1O), .clr(Reset));
  Register #(.width(32)) register_2 (.D(ALURes2), .en(clk), .clk(clk), .Q(ALUR2O), .clr(Reset));
  Register #(.width(2)) register_3 (.D(BranchtoPC), .en(clk), .clk(clk), .Q(BTPO), .clr(Reset));
  Register #(.width(1)) register_4 (.D(MemRd), .en(clk), .clk(clk), .Q(MRO), .clr(Reset));
  Register #(.width(1)) register_5 (.D(MemWr), .en(clk), .clk(clk), .Q(MWO), .clr(Reset));
  Register #(.width(2)) register_6 (.D(MemSMode), .en(clk), .clk(clk), .Q(MSMO), .clr(Reset));
  Register #(.width(3)) register_7 (.D(MemLMode), .en(clk), .clk(clk), .Q(MLMO), .clr(Reset));
  Register #(.width(32)) register_8 (.D(RegtoMem), .en(clk), .clk(clk), .Q(RTMO), .clr(Reset));
  Register #(.width(2)) register_9 (.D(WBSel), .en(clk), .clk(clk), .Q(WBSO), .clr(Reset));
  Register #(.width(1)) register_10 (.D(W_En), .en(clk), .clk(clk), .Q(WENO), .clr(Reset));
  Register #(.width(2)) register_11 (.D(JumpMode), .en(clk), .clk(clk), .Q(JMO), .clr(Reset));
  Register #(.width(2)) register_12 (.D(RegInstType), .en(clk), .clk(clk), .Q(RITO), .clr(Reset));
  Register #(.width(5)) register_13 (.D(W_Reg), .en(clk), .clk(clk), .Q(WRO), .clr(Reset));
endmodule

module MEM_Reg (
  input  clk,
  input  Reset,
  input  [31:0] ALURes1,
  input  [31:0] ALURes2,
  input  [31:0] MemtoWB,
  input  [1:0] WBSel,
  input  W_En,
  input  [1:0] JumpMode,
  input  [1:0] RegInstType,
  input  [4:0] W_Reg,
  output [31:0] ALUR1O,
  output [31:0] ALUR2O,
  output [31:0] MTWBO,
  output [1:0] WBSO,
  output WENO,
  output [1:0] JMO,
  output [1:0] RITO,
  output [4:0] WRO
);

  Register #(.width(32)) register_1 (.D(ALURes1), .en(clk), .clk(clk), .Q(ALUR1O), .clr(Reset));
  Register #(.width(32)) register_2 (.D(ALURes2), .en(clk), .clk(clk), .Q(ALUR2O), .clr(Reset));
  Register #(.width(32)) register_3 (.D(MemtoWB), .en(clk), .clk(clk), .Q(MTWBO), .clr(Reset));
  Register #(.width(2)) register_4 (.D(WBSel), .en(clk), .clk(clk), .Q(WBSO), .clr(Reset));
  Register #(.width(1)) register_5 (.D(W_En), .en(clk), .clk(clk), .Q(WENO), .clr(Reset));
  Register #(.width(2)) register_6 (.D(JumpMode), .en(clk), .clk(clk), .Q(JMO), .clr(Reset));
  Register #(.width(2)) register_7 (.D(RegInstType), .en(clk), .clk(clk), .Q(RITO), .clr(Reset));
  Register #(.width(5)) register_8 (.D(W_Reg), .en(clk), .clk(clk), .Q(WRO), .clr(Reset));
endmodule

module ConflictHandler (
  input  clk,
  input  [4:0] EX_WReg,
  input  [4:0] ID_RReg1,
  input  [4:0] ID_RReg2,
  input  [1:0] EX_InstType,
  input  [1:0] ID_InstType,
  input  Reset,
  output PauseIF,
  output PauseID,
  output PauseEx,
  output PauseWB
);

  wire and_1_out, and_2_out, comparator_1_eq, comparator_2_eq, comparator_3_lt, comparator_4_lt,
       comparator_5_eq, not_1_out, or_1_out, or_2_out;
  wire [1:0] multiplexer_1_out, register_1_q, subtractor_1_out;

  Comparator #(.mode("unsigned"), .width(5)) comparator_1 (
    .a(EX_WReg), .b(ID_RReg1), .eq(comparator_1_eq));  // open: gt, lt
  Comparator #(.mode("unsigned"), .width(5)) comparator_2 (
    .a(EX_WReg), .b(ID_RReg2), .eq(comparator_2_eq));  // open: gt, lt
  Comparator #(.mode("unsigned"), .width(2)) comparator_3 (
    .a(EX_InstType), .b(2'b10), .lt(comparator_3_lt));  // open: gt, eq
  Comparator #(.mode("unsigned"), .width(2)) comparator_4 (
    .a(ID_InstType), .b(2'b10), .lt(comparator_4_lt));  // open: gt, eq
  or or_1 (or_1_out, comparator_1_eq, comparator_2_eq);
  and and_1 (and_1_out, or_1_out, and_2_out);
  and and_2 (and_2_out, comparator_3_lt, comparator_4_lt);
  not not_1 (not_1_out, and_1_out);
  Comparator #(.mode("unsigned"), .width(2)) comparator_5 (
    .a(2'b00), .b(subtractor_1_out), .eq(comparator_5_eq));  // open: gt, lt
  or or_2 (or_2_out, not_1_out, comparator_5_eq);
  Register #(.width(2)) register_1 (.D(multiplexer_1_out), .en(1'b1), .clk(clk), .Q(register_1_q), .clr(Reset));
  Multiplexer #(.width(2)) multiplexer_1 (.in0(subtractor_1_out), .in1(2'b10), .out(multiplexer_1_out), .sel(or_2_out));
  Comparator #(.mode("unsigned"), .width(2)) comparator_6 (.a(register_1_q), .b(2'b10), .lt(PauseEx));  // open: gt, eq
  Subtractor #(.width(2)) subtractor_1 (.a(register_1_q), .b(2'b01), .out(subtractor_1_out));  // open: bin, bout

  assign PauseID = PauseEx;
  assign PauseIF = PauseEx;
endmodule

module IF_Ctrl (
  input  clk,
  input  Pause,
  output IF_clk
);

  Multiplexer multiplexer_1 (.in0(clk), .in1(1'b0), .out(IF_clk), .sel(Pause));
endmodule

module ID_Ctrl (
  input  clk1,
  input  clk2,
  input  Pause,
  output ID_clk1,
  output ID_clk2
);

  Multiplexer multiplexer_1 (.in0(clk1), .in1(1'b0), .out(ID_clk1), .sel(Pause));
  Multiplexer multiplexer_2 (.in0(clk2), .in1(1'b0), .out(ID_clk2), .sel(Pause));
endmodule

module Ex_Ctrl (
  input  clk,
  input  Pause,
  output Ex_clk
);

  Multiplexer multiplexer_1 (.in0(clk), .in1(1'b0), .out(Ex_clk), .sel(Pause));
endmodule

module MEM_Ctrl (
  input  clk,
  input  Pause,
  output MEM_clk
);

  Multiplexer multiplexer_1 (.in0(clk), .in1(1'b0), .out(MEM_clk), .sel(Pause));
endmodule
