// Logisim project register_group.circ as structural Verilog: 3 circuits, main circuit RAM32
module RAM32 (
  input  in_1,
  input  in_2,
  input  [7:0] in_3,
  input  clk,
  input  [31:0] in_5,
  output [31:0] out_6
);

  RAM #(.dataWidth(32)) ram_1 (.addr(in_3), .we(in_2), .oe(in_1), .clk(clk), .din(in_5), .dout(out_6));
endmodule

module register_group16 (
  input  clk,
  input  [31:0] W_data,
  input  W_En,
  input  [3:0] W_Reg,
  input  [3:0] R_Reg1,
  input  [3:0] R_Reg2,
  output [31:0] R_data1,
  output [31:0] R_data2
);

  wire decoder_1_out0, decoder_1_out1, decoder_1_out2, decoder_1_out3, decoder_1_out4, decoder_1_out5,
       decoder_1_out6, decoder_1_out7, decoder_1_out8, decoder_1_out9, decoder_1_out10, decoder_1_out11,
       decoder_1_out12, decoder_1_out13, decoder_1_out14, decoder_1_out15;
  wire [31:0] register_1_q, register_2_q, register_3_q, register_4_q, register_5_q, register_6_q,
       register_7_q, register_8_q, register_9_q, register_10_q, register_11_q, register_12_q, register_13_q,
       register_14_q, register_15_q, register_16_q;

  Decoder #(.select(4)) decoder_1 (
    .out0(decoder_1_out0), .out1(decoder_1_out1), .out2(decoder_1_out2), .out3(decoder_1_out3),
    .out4(decoder_1_out4), .out5(decoder_1_out5), .out6(decoder_1_out6), .out7(decoder_1_out7),
    .out8(decoder_1_out8), .out9(decoder_1_out9), .out10(decoder_1_out10), .out11(decoder_1_out11),
    .out12(decoder_1_out12), .out13(decoder_1_out13), .out14(decoder_1_out14), .out15(decoder_1_out15),
    .sel(W_Reg), .en(W_En));
  Register #(.width(32)) register_1 (.D(W_data), .en(decoder_1_out0), .clk(clk), .Q(register_1_q));  // open: clr
  Register #(.width(32)) register_2 (.D(W_data), .en(decoder_1_out1), .clk(clk), .Q(register_2_q));  // open: clr
  Register #(.width(32)) register_3 (.D(W_data), .en(decoder_1_out2), .clk(clk), .Q(register_3_q));  // open: clr
  Register #(.width(32)) register_4 (.D(W_data), .en(decoder_1_out3), .clk(clk), .Q(register_4_q));  // open: clr
  Register #(.width(32)) register_5 (.D(W_data), .en(decoder_1_out4), .clk(clk), .Q(register_5_q));  // open: clr
  Register #(.width(32)) register_6 (.D(W_data), .en(decoder_1_out5), .clk(clk), .Q(register_6_q));  // open: clr
  Register #(.width(32)) register_7 (.D(W_data), .en(decoder_1_out6), .clk(clk), .Q(register_7_q));  // open: clr
  Register #(.width(32)) register_8 (.D(W_data), .en(decoder_1_out7), .clk(clk), .Q(register_8_q));  // open: clr
  Register #(.width(32)) register_9 (.D(W_data), .en(decoder_1_out8), .clk(clk), .Q(register_9_q));  // open: clr
  Register #(.width(32)) register_10 (.D(W_data), .en(decoder_1_out9), .clk(clk), .Q(register_10_q));  // open: clr
  Register #(.width(32)) register_11 (.D(W_data), .en(decoder_1_out10), .clk(clk), .Q(register_11_q));  // open: clr
  Register #(.width(32)) register_12 (.D(W_data), .en(decoder_1_out11), .clk(clk), .Q(register_12_q));  // open: clr
  Register #(.width(32)) register_13 (.D(W_data), .en(decoder_1_out12), .clk(clk), .Q(register_13_q));  // open: clr
  Register #(.width(32)) register_14 (.D(W_data), .en(decoder_1_out13), .clk(clk), .Q(register_14_q));  // open: clr
  Register #(.width(32)) register_15 (.D(W_data), .en(decoder_1_out14), .clk(clk), .Q(register_15_q));  // open: clr
  Register #(.width(32)) register_16 (.D(W_data), .en(decoder_1_out15), .clk(clk), .Q(register_16_q));  // open: clr
  Multiplexer #(.select(4), .width(32)) multiplexer_1 (
    .in0(register_1_q), .in1(register_2_q), .in2(register_3_q), .in3(register_4_q), .in4(register_5_q),
    .in5(register_6_q), .in6(register_7_q), .in7(register_8_q), .in8(register_9_q), .in9(register_10_q),
    .in10(register_11_q), .in11(register_12_q), .in12(register_13_q), .in13(register_14_q),
    .in14(register_15_q), .in15(register_16_q), .out(R_data1), .sel(R_Reg1));
  Multiplexer #(.select(4), .width(32)) multiplexer_2 (
    .in0(register_1_q), .in1(register_2_q), .in2(register_3_q), .in3(register_4_q), .in4(register_5_q),
    .in5(register_6_q), .in6(register_7_q), .in7(register_8_q), .in8(register_9_q), .in9(register_10_q),
    .in10(register_11_q), .in11(register_12_q), .in12(register_13_q), .in13(register_14_q),
    .in14(register_15_q), .in15(register_16_q), .out(R_data2), .sel(R_Reg2));
endmodule

module register_group32 (
  input  clk,
  input  W_En,
  input  [31:0] W_data,
  input  [4:0] W_Reg,
  input  [4:0] R_Reg1,
  input  [4:0] R_Reg2,
  output [31:0] R_data1,
  output [31:0] R_data2
);

  wire and_1_out, and_2_out, bitselector_2_out, bitselector_4_out, bitselector_6_out, not_1_out;
  wire [3:0] bitselector_1_out, bitselector_3_out, bitselector_5_out;
  wire [31:0] register_group16_1_r_data1, register_group16_1_r_data2, register_group16_2_r_data1,
       register_group16_2_r_data2;

  BitSelector #(.group(4), .width(5)) bitselector_1 (.in(W_Reg), .out(bitselector_1_out), .sel(1'b0));
  BitSelector #(.width(5)) bitselector_2 (.in(W_Reg), .out(bitselector_2_out), .sel(3'b100));
  BitSelector #(.group(4), .width(5)) bitselector_3 (.in(R_Reg1), .out(bitselector_3_out), .sel(1'b0));
  BitSelector #(.width(5)) bitselector_4 (.in(R_Reg1), .out(bitselector_4_out), .sel(3'b100));
  BitSelector #(.group(4), .width(5)) bitselector_5 (.in(R_Reg2), .out(bitselector_5_out), .sel(1'b0));
  BitSelector #(.width(5)) bitselector_6 (.in(R_Reg2), .out(bitselector_6_out), .sel(3'b100));
  not not_1 (not_1_out, bitselector_2_out);
  and and_1 (and_1_out, W_En, not_1_out);
  and and_2 (and_2_out, W_En, bitselector_2_out);
  register_group16 register_group16_1 (
    .clk(clk), .W_data(W_data), .W_En(and_1_out), .W_Reg(bitselector_1_out), .R_Reg1(bitselector_3_out),
    .R_Reg2(bitselector_5_out), .R_data1(register_group16_1_r_data1), .R_data2(register_group16_1_r_data2));
  register_group16 register_group16_2 (
    .clk(clk), .W_data(W_data), .W_En(and_2_out), .W_Reg(bitselector_1_out), .R_Reg1(bitselector_3_out),
    .R_Reg2(bitselector_5_out), .R_data1(register_group16_2_r_data1), .R_data2(register_group16_2_r_data2));
  Multiplexer #(.width(32)) multiplexer_1 (
    .in0(register_group16_1_r_data1), .in1(register_group16_2_r_data1), .out(R_data1), .sel(bitselector_4_out));
  Multiplexer #(.width(32)) multiplexer_2 (
    .in0(register_group16_1_r_data2), .in1(register_group16_2_r_data2), .out(R_data2), .sel(bitselector_6_out));
endmodule
